# Fritzing sketch MultiButton (saved by Fritzing 0.7.7b)
breadboards: 1

parts:
  S1 = Pushbutton [package=THT]
  R1 = Resistor [resistance=10k tolerance=±5% package=THT]
  LED1 = LED - 5mm [color="Red (633nm)" package="5 mm [THT]"]
  Arduino2 = Arduino
  S2 = Pushbutton [package=THT]
  S3 = Pushbutton [package=THT]
  R2 = Resistor [resistance=10k tolerance=±5% package=THT]
  R3 = Resistor [resistance=10k tolerance=±5% package=THT]

nets (from the breadboard view):
  N1: S1.leg0, Arduino2.+5V, S2.leg0
  N2: S1.leg1, R1.Pin_1, Arduino2.D8
  N3: R1.Pin_0, LED1.cathode, Arduino2.GND, R2.Pin_0, R3.Pin_0
  N4: LED1.anode, Arduino2.D13
  N5: S2.leg1, R2.Pin_1
  N6: S3.leg1, R3.Pin_1

notes:
  In this example, a pushbutton is used as a digital input and an LED is a digital output. Related example: http://arduino.cc/en/Tutorial/Button
